# Fritzing sketch selfmadecul (saved by Fritzing 0.9.3b)
circuit board: 3.5cm x 9cm
breadboards: 1

parts:
  R1 = Resistor [tolerance=±5% resistance=220 package=THT]
  LED1 = LED - 5mm [color="Red (633nm)" package="5 mm [THT]"]
  R2 = Resistor [tolerance=±5% resistance=420 package=THT]
  R3 = Resistor [tolerance=±5% resistance=1k package=THT]
  R4 = Resistor [tolerance=±5% resistance=420 package=THT]
  R5 = Resistor [tolerance=±5% resistance=1k package=THT]
  R7 = Resistor [tolerance=±5% resistance=1k package=THT]
  R8 = Resistor [tolerance=±5% resistance=10k package=THT]
  J1 = female pin header, 8 pins [form="♀ (female)"]
  Bauteil1 = Arduino Nano (Rev3.0)
  R6 = Resistor [tolerance=±5% resistance=420 package=THT]

nets:
  N1: R1.Pin_0, Bauteil1.D9
  N2: R1.Pin_1, LED1.anode
  GND: LED1.cathode, R3.Pin_1, R5.Pin_1, R7.Pin_1, J1.pin2, Bauteil1.GND
  N3: R2.Pin_0, Bauteil1.D11/MOSI
  MOSI: R2.Pin_1, R3.Pin_0, J1.pin3
  N4: R4.Pin_0, Bauteil1.D13/SCK
  SCLK: R4.Pin_1, R5.Pin_0, J1.pin4
  CSN: R7.Pin_0, R8.Pin_1, J1.pin8, R6.Pin_1
  3.3V: R8.Pin_0, J1.pin1, Bauteil1.3V3
  MISO: J1.pin5, Bauteil1.D12/MISO
  GDO2: J1.pin6, Bauteil1.D2
  GDO0: J1.pin7, Bauteil1.D3
  N5: Bauteil1.D10, R6.Pin_0
